// Digital circuit XOR3_new.dig as structural Verilog
module XOR3_new (
  input  A,
  input  B,
  input  C,
  output Y
);

  wire and_1_out, and_2_out, and_3_out, and_4_out, not_1_out, not_2_out, not_3_out, not_4_out, not_5_out,
       not_6_out;

  not not_1 (not_1_out, B);
  not not_2 (not_2_out, C);
  not not_3 (not_3_out, A);
  not not_4 (not_4_out, A);
  not not_5 (not_5_out, C);
  not not_6 (not_6_out, B);
  and and_1 (and_1_out, A, not_1_out, not_2_out);
  and and_2 (and_2_out, not_4_out, B, not_5_out);
  and and_3 (and_3_out, not_3_out, not_6_out, C);
  and and_4 (and_4_out, A, B, C);
  or or_1 (Y, and_1_out, and_2_out, and_3_out, and_4_out);
endmodule
