// Digital circuit full_adder_orig.dig as structural Verilog
module full_adder_orig (
  input  A,
  input  B,
  input  C_in,
  output C_out,
  output Y
);

  wire and_1_out, and_2_out, xor_1_out;

  xor xor_1 (xor_1_out, A, B);
  xor xor_2 (Y, xor_1_out, C_in);
  and and_1 (and_1_out, C_in, xor_1_out);
  and and_2 (and_2_out, B, A);
  or or_1 (C_out, and_1_out, and_2_out);
endmodule
