// Digital circuit half_adder_new.dig as structural Verilog
module half_adder_new (
  input  A,
  input  B,
  output Y,
  output C
);

  wire and_1_out, and_2_out, not_1_out, not_2_out;

  and and_1 (and_1_out, A, not_1_out);
  not not_1 (not_1_out, B);
  and and_2 (and_2_out, not_2_out, B);
  not not_2 (not_2_out, A);
  or or_1 (Y, and_1_out, and_2_out);
  and and_3 (C, A, B);
endmodule
