// Digital circuit 2bit_adder.dig as structural Verilog
module _2bit_adder (
  input  A_0,
  input  B_0,
  input  A_1,
  input  B_1,
  output Y_0,
  output Y_1,
  output C
);

  wire full_adder_new_2_c_out;

  full_adder_new full_adder_new_1 (.A(A_1), .B(B_1), .C_in(full_adder_new_2_c_out), .Y(Y_1), .C_out(C));
  full_adder_new full_adder_new_2 (.A(A_0), .B(B_0), .C_in(1'b0), .Y(Y_0), .C_out(full_adder_new_2_c_out));
endmodule
