// Digital circuit multiply.dig as structural Verilog
module multiply (
  input  Y_in,
  input  X_in,
  output Y_out,
  output X_out
);

  and and_1 (X_out, Y_in, X_in);

  assign Y_out = Y_in;
endmodule
