// Digital circuit neg_multiply.dig as structural Verilog
module neg_multiply (
  input  Y_in,
  input  X_in,
  output Y_out,
  output X_out
);

  wire not_1_out;

  not not_1 (not_1_out, Y_in);
  and and_1 (X_out, X_in, not_1_out);

  assign Y_out = Y_in;
endmodule
