// Digital circuit full_adder_new.dig as structural Verilog
module full_adder_new (
  input  A,
  input  B,
  input  C_in,
  output Y,
  output C_out
);

  wire adder_1_y_out, adder_2_y_out, adder_3_y_out, adder_5_y_out, adder_6_y_out, identer_1_x_out,
       identer_1_y_out, identer_2_x_out, identer_3_x_out, identer_3_y_out, multiply_1_x_out,
       multiply_1_y_out, multiply_2_x_out, multiply_2_y_out, multiply_3_x_out, multiply_3_y_out,
       multiply_4_x_out, multiply_4_y_out, multiply_5_x_out, multiply_5_y_out, multiply_6_x_out,
       multiply_6_y_out, multiply_7_x_out, multiply_7_y_out, multiply_8_x_out, multiply_8_y_out,
       multiply_9_x_out, multiply_9_y_out, multiply_10_x_out, multiply_10_y_out, multiply_11_x_out,
       multiply_12_x_out, neg_multiply_1_x_out, neg_multiply_1_y_out, neg_multiply_2_x_out,
       neg_multiply_2_y_out, neg_multiply_3_x_out, neg_multiply_3_y_out, neg_multiply_4_x_out,
       neg_multiply_4_y_out, neg_multiply_5_x_out, neg_multiply_5_y_out, neg_multiply_6_x_out,
       neg_multiply_6_y_out;

  neg_multiply neg_multiply_1 (.Y_out(neg_multiply_1_y_out), .X_out(neg_multiply_1_x_out), .Y_in(A), .X_in(1'b1));
  neg_multiply neg_multiply_2 (
    .Y_out(neg_multiply_2_y_out), .X_out(neg_multiply_2_x_out), .Y_in(B), .X_in(neg_multiply_1_x_out));
  multiply multiply_1 (.Y_out(multiply_1_y_out), .Y_in(C_in), .X_out(multiply_1_x_out), .X_in(neg_multiply_2_x_out));
  adder adder_1 (.Y_out(adder_1_y_out), .Y_in(1'b0), .X_in(multiply_1_x_out));  // open: X_out
  neg_multiply neg_multiply_3 (
    .Y_out(neg_multiply_3_y_out), .X_out(neg_multiply_3_x_out), .Y_in(neg_multiply_1_y_out), .X_in(1'b1));
  multiply multiply_2 (.Y_out(multiply_2_y_out), .Y_in(neg_multiply_3_y_out), .X_out(multiply_2_x_out), .X_in(1'b1));
  multiply multiply_3 (
    .Y_out(multiply_3_y_out), .Y_in(neg_multiply_2_y_out), .X_out(multiply_3_x_out),
    .X_in(neg_multiply_3_x_out));
  neg_multiply neg_multiply_4 (
    .Y_out(neg_multiply_4_y_out), .X_out(neg_multiply_4_x_out), .Y_in(multiply_3_y_out),
    .X_in(multiply_2_x_out));
  neg_multiply neg_multiply_5 (
    .Y_out(neg_multiply_5_y_out), .X_out(neg_multiply_5_x_out), .Y_in(multiply_1_y_out),
    .X_in(multiply_3_x_out));
  neg_multiply neg_multiply_6 (
    .Y_out(neg_multiply_6_y_out), .X_out(neg_multiply_6_x_out), .Y_in(neg_multiply_5_y_out),
    .X_in(neg_multiply_4_x_out));
  adder adder_2 (.Y_out(adder_2_y_out), .Y_in(adder_1_y_out), .X_in(neg_multiply_5_x_out));  // open: X_out
  adder adder_3 (.Y_out(adder_3_y_out), .Y_in(adder_2_y_out), .X_in(neg_multiply_6_x_out));  // open: X_out
  multiply multiply_4 (.Y_out(multiply_4_y_out), .Y_in(multiply_2_y_out), .X_out(multiply_4_x_out), .X_in(1'b1));
  multiply multiply_5 (
    .Y_out(multiply_5_y_out), .Y_in(neg_multiply_4_y_out), .X_out(multiply_5_x_out), .X_in(multiply_4_x_out));
  multiply multiply_6 (
    .Y_out(multiply_6_y_out), .Y_in(neg_multiply_6_y_out), .X_out(multiply_6_x_out), .X_in(multiply_5_x_out));
  adder adder_4 (.Y_out(Y), .Y_in(adder_3_y_out), .X_in(multiply_6_x_out));  // open: X_out
  multiply multiply_7 (.Y_out(multiply_7_y_out), .Y_in(multiply_4_y_out), .X_out(multiply_7_x_out), .X_in(1'b1));
  identer identer_1 (
    .Y_out(identer_1_y_out), .Y_in(multiply_5_y_out), .X_out(identer_1_x_out), .X_in(multiply_7_x_out));
  multiply multiply_8 (
    .Y_out(multiply_8_y_out), .Y_in(multiply_6_y_out), .X_out(multiply_8_x_out), .X_in(identer_1_x_out));
  adder adder_5 (.Y_out(adder_5_y_out), .Y_in(1'b0), .X_in(multiply_8_x_out));  // open: X_out
  multiply multiply_9 (.Y_out(multiply_9_y_out), .Y_in(multiply_7_y_out), .X_out(multiply_9_x_out), .X_in(1'b1));
  identer identer_2 (.Y_in(multiply_9_y_out), .X_out(identer_2_x_out), .X_in(1'b1));  // open: Y_out
  multiply multiply_10 (
    .Y_out(multiply_10_y_out), .Y_in(identer_1_y_out), .X_out(multiply_10_x_out), .X_in(multiply_9_x_out));
  multiply multiply_11 (.Y_in(multiply_10_y_out), .X_out(multiply_11_x_out), .X_in(identer_2_x_out));  // open: Y_out
  identer identer_3 (
    .Y_out(identer_3_y_out), .Y_in(multiply_8_y_out), .X_out(identer_3_x_out), .X_in(multiply_10_x_out));
  multiply multiply_12 (.Y_in(identer_3_y_out), .X_out(multiply_12_x_out), .X_in(multiply_11_x_out));  // open: Y_out
  adder adder_6 (.Y_out(adder_6_y_out), .Y_in(adder_5_y_out), .X_in(identer_3_x_out));  // open: X_out
  adder adder_7 (.Y_out(C_out), .Y_in(adder_6_y_out), .X_in(multiply_12_x_out));  // open: X_out
endmodule
