// Digital circuit bubble3.dig as structural Verilog
module bubble3 (
  input  A,
  input  B,
  input  E,
  input  D,
  input  C,
  output Y
);

  wire and_1_out, and_2_out, not_1_out, not_2_out, or_1_out;

  not not_1 (not_1_out, B);
  not not_2 (not_2_out, D);
  and and_1 (and_1_out, A, not_1_out);
  or or_1 (or_1_out, not_2_out, E);
  and and_2 (and_2_out, and_1_out, C);
  or or_2 (Y, and_2_out, or_1_out);
endmodule
