// Digital circuit kmap1-1.dig as structural Verilog
module kmap1_1 (
  input  A,
  input  B,
  input  C,
  output Y
);

  wire and_1_out, and_2_out, not_1_out;

  not not_1 (not_1_out, B);
  and and_1 (and_1_out, A, C);
  and and_2 (and_2_out, not_1_out, C);
  or or_1 (Y, and_1_out, and_2_out);
endmodule
