// Digital circuit kmap2-2.dig as structural Verilog
module kmap2_2 (
  input  A,
  input  B,
  input  C,
  input  D,
  output Y
);

  wire and_1_out;

  and and_1 (and_1_out, C, D);
  or or_1 (Y, A, B, and_1_out);
endmodule
