// Digital circuit D-latch.dig as structural Verilog
module D_latch (
  input  CLK,
  input  D,
  output Q,
  output Qb
);

  wire and_1_out, and_2_out, not_1_out;

  not not_1 (not_1_out, D);
  and and_1 (and_1_out, CLK, not_1_out);
  and and_2 (and_2_out, CLK, D);
  nor nor_1 (Q, and_1_out, Qb);
  nor nor_2 (Qb, Q, and_2_out);
endmodule

/* Test case:
CLK D Q Qb
1 0 0 1
0 0 0 1
1 0 0 1
0 0 0 1
0 1 0 1
1 1 1 0
0 1 1 0
0 0 1 0
1 0 0 1
*/
