// Digital circuit D-Latch_vs_D-Flipflop.dig as structural Verilog
module D_Latch_vs_D_Flipflop (
  input  D,
  input  CLK,
  output Q_FlipFlop,
  output Q_Latch
);

  wire and_1_out, and_2_out, and_3_out, and_4_out, and_5_out, and_6_out, nor_1_out, nor_2_out, nor_4_out,
       nor_6_out, not_1_out, not_2_out, not_3_out, not_4_out;

  not not_1 (not_1_out, D);
  and and_1 (and_1_out, CLK, not_1_out);
  and and_2 (and_2_out, CLK, D);
  not not_2 (not_2_out, D);
  and and_3 (and_3_out, CLK, not_2_out);
  and and_4 (and_4_out, CLK, D);
  nor nor_1 (nor_1_out, and_1_out, nor_2_out);
  nor nor_2 (nor_2_out, nor_1_out, and_2_out);
  nor nor_3 (Q_Latch, and_3_out, nor_4_out);
  nor nor_4 (nor_4_out, Q_Latch, and_4_out);
  not not_3 (not_3_out, CLK);
  not not_4 (not_4_out, nor_1_out);
  and and_5 (and_5_out, not_3_out, not_4_out);
  and and_6 (and_6_out, not_3_out, nor_1_out);
  nor nor_5 (Q_FlipFlop, and_5_out, nor_6_out);
  nor nor_6 (nor_6_out, Q_FlipFlop, and_6_out);

  // Notes on the sheet:
  //   D
  //   CLK
endmodule

/* Test case:
D CLK Q_FlipFlop Q_Latch
0 1   x x
1 1   x x
1 0   x x
1 1   x x
0 1   x x
1 1   x x
1 0   x x
0 0   x x
1 0   x x
1 1   x x
*/
