// Digital circuit fair_coffee_machine.dig as structural Verilog
module fair_coffee_machine (
  input  clk
);

  wire A_out, and_1_out, and_2_out, and_3_out, and_4_out, and_5_out, and_6_out, and_7_out, and_8_out,
       and_9_out, and_10_out, and_11_out, and_12_out, and_13_out, and_14_out, and_15_out, B1_out, B2_out,
       not_1_out, not_2_out, not_3_out, not_4_out, not_5_out, or_1_out, or_2_out, or_3_out, or_4_out, S0_q,
       S1_q;

  Button A (.out(A_out));
  not not_1 (not_1_out, A_out);
  Button B1 (.out(B1_out));
  Button B2 (.out(B2_out));
  not not_2 (not_2_out, B1_out);
  not not_3 (not_3_out, B2_out);
  not not_4 (not_4_out, S0_q);
  not not_5 (not_5_out, S1_q);
  and and_1 (and_1_out, A_out, not_4_out, not_5_out);
  and and_2 (and_2_out, not_1_out, not_2_out, S0_q, not_5_out);
  and and_3 (and_3_out, not_1_out, B1_out, not_3_out, not_4_out, S1_q);
  and and_4 (and_4_out, A_out, S0_q, not_5_out);
  and and_5 (and_5_out, A_out, not_4_out, S1_q);
  and and_6 (and_6_out, not_1_out, not_2_out, not_3_out, not_4_out, S1_q);
  and and_7 (and_7_out, not_1_out, B1_out, S0_q, not_5_out);
  and and_8 (and_8_out, not_1_out, B1_out, not_3_out, not_4_out, S1_q);
  and and_9 (and_9_out, not_1_out, B2_out, not_4_out, S1_q);
  and and_10 (and_10_out, A_out, not_4_out, S1_q);
  and and_11 (and_11_out, A_out, S0_q, not_5_out);
  and and_12 (and_12_out, not_1_out, not_2_out, S0_q, not_5_out);
  and and_13 (and_13_out, A_out, not_4_out, S1_q);
  and and_14 (and_14_out, not_1_out, B1_out, not_3_out, not_4_out, S1_q);
  and and_15 (and_15_out, not_1_out, not_2_out, not_3_out, not_4_out, S1_q);
  or or_1 (or_1_out, and_1_out, and_2_out, and_3_out);
  or or_2 (or_2_out, and_4_out, and_5_out, and_6_out);
  or or_3 (or_3_out, and_7_out, and_8_out);
  or or_4 (or_4_out, and_11_out, and_12_out, and_13_out, and_14_out, and_15_out);
  D_FF S0 (.D(or_1_out), .C(clk), .Q(S0_q));  // open: nQ
  D_FF S1 (.D(or_2_out), .C(clk), .Q(S1_q));  // open: nQ
  LED Y1 (.in(or_4_out));
  LED Y2 (.in(or_3_out));
  LED Y3 (.in(and_9_out));
  LED Y4 (.in(and_10_out));
  LED S1_2 (.in(S1_q));
  LED S0_2 (.in(S0_q));

  // Notes on the sheet:
  //   S0
  //   S1
endmodule
