// Digital circuit fancy_coffee_machine.dig as structural Verilog
module fancy_coffee_machine (
  input  clk
);

  wire and_1_out, and_2_out, and_3_out, and_4_out, and_5_out, and_6_out, and_7_out, and_8_out, and_9_out,
       and_10_out, and_11_out, and_12_out, and_13_out, and_14_out, and_15_out, and_16_out, and_17_out,
       and_18_out, and_19_out, and_20_out, and_21_out, and_22_out, and_23_out, and_24_out, and_25_out,
       and_26_out, and_27_out, and_28_out, and_29_out, Coin_out, Large_Coffee_out, Latte_Macchiato_out,
       not_1_out, not_2_out, not_3_out, not_4_out, not_5_out, not_6_out, or_1_out, or_2_out, or_3_out,
       or_4_out, or_5_out, S0_q, S1_2_q, Small_Coffee_out;

  Button Coin (.out(Coin_out));
  Button Small_Coffee (.out(Small_Coffee_out));
  not not_1 (not_1_out, Coin_out);
  Button Large_Coffee (.out(Large_Coffee_out));
  not not_2 (not_2_out, Small_Coffee_out);
  Button Latte_Macchiato (.out(Latte_Macchiato_out));
  not not_3 (not_3_out, Large_Coffee_out);
  not not_4 (not_4_out, Latte_Macchiato_out);
  not not_5 (not_5_out, S0_q);
  not not_6 (not_6_out, S1_2_q);
  and and_1 (and_1_out, Coin_out, not_5_out, not_6_out);
  and and_2 (and_2_out, not_1_out, not_2_out, S0_q, not_6_out);
  and and_3 (and_3_out, Coin_out, not_5_out, S1_2_q);
  and and_4 (and_4_out, not_1_out, Small_Coffee_out, not_3_out, not_5_out, S1_2_q);
  and and_5 (and_5_out, Coin_out, S0_q, S1_2_q);
  and and_6 (and_6_out, not_1_out, Large_Coffee_out, not_4_out, S0_q, S1_2_q);
  and and_7 (and_7_out, not_1_out, not_2_out, not_3_out, not_4_out, S0_q, S1_2_q);
  and and_8 (and_8_out, Coin_out, S0_q, not_6_out);
  and and_9 (and_9_out, Coin_out, not_5_out, S1_2_q);
  and and_10 (and_10_out, not_1_out, not_2_out, not_3_out, not_5_out, S1_2_q);
  and and_11 (and_11_out, Coin_out, S0_q, S1_2_q);
  and and_12 (and_12_out, not_1_out, Small_Coffee_out, not_3_out, not_4_out, S0_q, S1_2_q);
  and and_13 (and_13_out, not_1_out, not_2_out, not_3_out, not_4_out, S0_q, S1_2_q);
  and and_14 (and_14_out, Coin_out, S0_q, not_6_out);
  and and_15 (and_15_out, not_1_out, not_2_out, S0_q, not_6_out);
  and and_16 (and_16_out, Coin_out, not_5_out, S1_2_q);
  and and_17 (and_17_out, not_1_out, Small_Coffee_out, not_3_out, not_5_out, S1_2_q);
  and and_18 (and_18_out, not_1_out, not_2_out, not_3_out, not_5_out, S1_2_q);
  and and_19 (and_19_out, Coin_out, S0_q, S1_2_q);
  and and_20 (and_20_out, not_1_out, Small_Coffee_out, not_3_out, not_4_out, S0_q, S1_2_q);
  and and_21 (and_21_out, not_1_out, Large_Coffee_out, not_4_out, S0_q, S1_2_q);
  and and_22 (and_22_out, not_1_out, not_2_out, not_3_out, not_4_out, S0_q, S1_2_q);
  and and_23 (and_23_out, not_1_out, Small_Coffee_out, S0_q, not_6_out);
  and and_24 (and_24_out, not_1_out, Small_Coffee_out, not_3_out, not_5_out, S1_2_q);
  and and_25 (and_25_out, not_1_out, Small_Coffee_out, not_3_out, not_4_out, S0_q, S1_2_q);
  and and_26 (and_26_out, not_1_out, Large_Coffee_out, not_5_out, S1_2_q);
  and and_27 (and_27_out, not_1_out, Large_Coffee_out, not_4_out, S0_q, S1_2_q);
  and and_28 (and_28_out, not_1_out, Latte_Macchiato_out, S0_q, S1_2_q);
  and and_29 (and_29_out, Coin_out, S0_q, S1_2_q);
  or or_1 (or_1_out, and_1_out, and_2_out, and_3_out, and_4_out, and_5_out, and_6_out, and_7_out);
  or or_2 (or_2_out, and_8_out, and_9_out, and_10_out, and_11_out, and_12_out, and_13_out);
  or or_3 (or_3_out, and_14_out, and_15_out, and_16_out, and_17_out, and_18_out, and_19_out, and_20_out, and_21_out, and_22_out);
  or or_4 (or_4_out, and_23_out, and_24_out, and_25_out);
  or or_5 (or_5_out, and_26_out, and_27_out);
  LED Ready (.in(or_3_out));
  LED Brew_Small_Coffee (.in(or_4_out));
  LED Brew_Large_Coffee (.in(or_5_out));
  LED Brew_Latte_Macchiato (.in(and_28_out));
  LED Return_Coin (.in(and_29_out));
  LED S1 (.in(S1_2_q));
  D_FF S0 (.D(or_1_out), .C(clk), .Q(S0_q));  // open: nQ
  D_FF S1_2 (.D(or_2_out), .C(clk), .Q(S1_2_q));  // open: nQ
  LED S0_2 (.in(S0_q));

  // Notes on the sheet:
  //   S0
  //   S1
endmodule
