// Digital circuit simple_coffee_machine.dig as structural Verilog
module simple_coffee_machine (
  input  Button,
  input  Coin,
  input  CLK
);

  wire and_1_out, and_2_out, and_3_out, not_1_out, or_1_out, S0_nq, S0_q;

  not not_1 (not_1_out, Button);
  and and_1 (and_1_out, not_1_out, S0_q);
  and and_2 (and_2_out, Coin, S0_nq);
  and and_3 (and_3_out, S0_q, Button);
  or or_1 (or_1_out, and_1_out, and_2_out);
  D_FF S0 (.D(or_1_out), .C(CLK), .Q(S0_q), .nQ(S0_nq));
  LED Ready (.in(S0_q));
  LED Brew_Coffee (.in(and_3_out));
endmodule
